// Logisim project Line_following_maze_solver.circ as structural Verilog: 4 circuits, main circuit main
module main (
  output [4:0] Counter
);

  wire _1, _2, _3, _4, _5, _6, _7, _8, _9, _10, _11, _12, _13, _14, _15, _16, _17, _18, _19, _20, Clock_out,
       LB, LF, LL, LR, RB, Reset_out, RF, RL, RR, S_0, S_1, S_2, S_3, S_4, undriven;
  wire [3:0] path_generator_1_lsrb;

  Button Clock (.out(Clock_out));
  Button Reset (.out(Reset_out));
  path_generator path_generator_1 (
    .Button(Clock_out), .Reset(Reset_out), .Counter(Counter), .LSRB(path_generator_1_lsrb));  // open: _1_S, _2_L, _3_S, _4_R, _5_S, _6_L, _7_S, _8_L, _9_S, _10_B, _11_S, _12_L, _13_S, _14_L, _15_S, _16_L, _17_S, _18_R, _19_S, _20_Stop
  Driver_system driver_system_1 (
    .L(path_generator_1_lsrb[3]), .S(path_generator_1_lsrb[2]), .R(path_generator_1_lsrb[1]),
    .B(path_generator_1_lsrb[0]), .S_0(S_0), .LF(LF), .S_1(S_1), .LB(LB), .S_2(S_2), .LR(LR), .LL(LL),
    .S_3(S_3), .RF(RF), .RB(RB), .S_4(S_4), .RR(RR), .RL(RL));  // open: a, b_2, c, d, e
  LED led_1 ();  // open: in
  LED led_2 (.in(_14));
  LED led_3 (.in(_15));
  LED led_4 (.in(undriven));
  LED led_5 (.in(_13));
  LED led_6 (.in(_16));
  LED led_7 (.in(_13));
  LED led_8 (.in(_17));
  LED led_9 (.in(_18));
  LED led_10 (.in(_19));
  LED led_11 (.in(_20));
  LED led_12 ();  // open: in
  LED led_13 (.in(LF));
  LED led_14 (.in(LB));
  LED led_15 (.in(LR));
  LED led_16 (.in(LL));
  LED led_17 (.in(_12));
  LED led_18 (.in(_11));
  LED led_19 (.in(_11));
  LED led_20 (.in(_8));
  LED led_21 (.in(_9));
  LED led_22 (.in(_10));
  LED led_23 (.in(S_4));
  LED led_24 ();  // open: in
  LED led_25 (.in(_7));
  LED led_26 (.in(S_0));
  LED led_27 (.in(S_2));
  LED led_28 (.in(_6));
  LED led_29 (.in(_5));
  LED led_30 (.in(_4));
  LED led_31 (.in(S_1));
  LED led_32 (.in(S_3));
  LED led_33 (.in(_3));
  LED led_34 (.in(RF));
  LED led_35 (.in(RB));
  LED led_36 (.in(RR));
  LED led_37 (.in(RL));
  LED led_38 (.in(_2));
  LED led_39 (.in(_1));
  path u__1 (
    .S(_1), .L(_2), .S_2(_3), .R(_4), .S_3(_5), .L_2(_6), .Stop(_20), .S_10(_19), .R_2(_18), .S_9(_17),
    .L_6(_16), .S_8(_15), .L_5(_14), .S_7(_13), .L_4(_12), .S_6(_11), .B(_10), .S_5(_9), .L_3(_8), .S_4(_7),
    .Reset_2(Reset_out), .Button_2(Clock_out));
  LED led_40 ();  // open: in
  LED led_41 ();  // open: in

  // Notes on the sheet:
  //            PATH GENERATOR
  //   DRIVER SYSTEM
  //   STOP
  //   Left motor forward
  //   Left motor backward
  //   Left motor right
  //   Left motor left
  //   LEFT MOTOR
  //   LINE FOLLOWING MAZE SOLVER
  //   Sensor-4
  //   SENSOR SYSTEM 
  //   Sensor-0
  //   Sensor-2
  //   Sensor-1
  //   Sensor-3
  //   RIGHT MOTOR
  //             START
  //   Right motor forward
  //   Right motor right
  //   Right motor left
  //   Right motor backward
  //   PATH
  //      3.      High                 Low
  //   DESCRIPTION
  //   based on LSRB priority.
  //   creates a pre-defined path.
  //   line by the sensors.
  //   1. Press the reset button for the robot to start from initial position.
  //   INSTRUCTIONS 
  //   2. Apply clock pulse each time for the next move until the robot reaches 
  //   4.If clock pulse exceeds 32 times,the robot comes to the start position again.
  //   1. When at junction the robot follows LSRB(Left-Straight-Right-Back) priority.
  //   2.The path generator module generates the direction in which the robot has to move
  //   3.The path module stores all the directions given by the path generator module and
  //   4.The driver system decides the direction of motors based on the detection of black
  //   it's destination.
endmodule

module Driver_system (
  input  L,
  input  S,
  input  R,
  input  B,
  output S_0,
  output a,
  output LF,
  output S_1,
  output b_2,
  output LB,
  output S_2,
  output LR,
  output c,
  output LL,
  output d,
  output S_3,
  output RF,
  output e,
  output RB,
  output S_4,
  output RR,
  output RL
);

  wire and_1_out, and_2_out, and_3_out, and_4_out, and_5_out, and_6_out, and_7_out, and_8_out, and_9_out,
       and_10_out, and_11_out, and_12_out, and_13_out, and_14_out, and_15_out, and_16_out, and_17_out,
       and_18_out, and_19_out, and_21_out, not_1_out, not_2_out, not_3_out, not_4_out, not_5_out, not_6_out,
       not_7_out, not_8_out, not_9_out, not_10_out, not_11_out, not_12_out, not_13_out, not_14_out,
       not_15_out, not_16_out, not_17_out, not_18_out, not_19_out, not_20_out, not_21_out, or_1_out,
       or_2_out, or_3_out, or_4_out;

  not not_1 (not_1_out, S);
  not not_2 (not_2_out, R);
  not not_3 (not_3_out, B);
  not not_4 (not_4_out, L);
  and and_1 (and_1_out, L, not_1_out, not_2_out, not_3_out);
  and and_2 (and_2_out, L, S, not_2_out, not_3_out);
  and and_3 (and_3_out, L, not_1_out, R, not_3_out);
  and and_4 (and_4_out, L, B, not_1_out, not_2_out);
  and and_5 (and_5_out, L, B, R, not_1_out);
  and and_6 (and_6_out, L, S, B, not_2_out);
  and and_7 (and_7_out, not_3_out, L, S, R);
  and and_8 (and_8_out, L, S, R, B);
  and and_9 (and_9_out, S, not_2_out, not_3_out, not_4_out);
  and and_10 (and_10_out, S, R, not_4_out, not_3_out);
  and and_11 (and_11_out, S, B, not_4_out, not_2_out);
  and and_12 (and_12_out, S, not_4_out, B, R);
  and and_13 (and_13_out, R, not_4_out, not_1_out, not_3_out);
  and and_14 (and_14_out, not_4_out, not_1_out, B, R);
  or or_1 (or_1_out, and_1_out, and_2_out, and_3_out, and_4_out, and_5_out);
  or or_2 (or_2_out, and_9_out, and_10_out, and_11_out, and_12_out);
  or or_3 (or_3_out, and_13_out, and_14_out);
  and and_15 (and_15_out, B, not_4_out, not_1_out, not_2_out);
  or or_4 (or_4_out, or_1_out, and_6_out, and_7_out, and_8_out);
  not not_5 (not_5_out, or_4_out);
  not not_6 (not_6_out, or_3_out);
  not not_7 (not_7_out, and_15_out);
  not not_8 (not_8_out, or_2_out);
  and and_16 (and_16_out, or_2_out, not_5_out);
  not not_9 (not_9_out, or_4_out);
  not not_10 (not_10_out, or_2_out);
  and and_17 (and_17_out, not_5_out, not_6_out, not_7_out);
  and and_18 (and_18_out, not_5_out, not_8_out, not_7_out);
  and and_19 (and_19_out, not_5_out, not_8_out, or_3_out);
  or or_5 (S_0, and_16_out, and_17_out);
  or or_6 (S_1, and_18_out, and_19_out);
  and and_20 (S_3, not_9_out, not_10_out, not_6_out, not_7_out);
  and and_21 (and_21_out, not_10_out, not_6_out, not_7_out);
  or or_7 (S_4, and_21_out, or_4_out);
  or or_8 (S_2, S_0, S_1, and_15_out, S_3, S_4);
  not not_11 (not_11_out, S_3);
  not not_12 (not_12_out, S_4);
  not not_13 (not_13_out, S_0);
  not not_14 (not_14_out, S_1);
  and and_22 (a, S_0, S_2, not_11_out, not_12_out);
  and and_23 (b_2, S_0, S_1, S_2, S_3, S_4);
  and and_24 (c, S_2, not_11_out, S_4);
  and and_25 (d, S_1, S_2, not_11_out, not_12_out, not_13_out);
  and and_26 (e, S_2, not_13_out, not_11_out, not_12_out, not_14_out);
  not not_15 (not_15_out, b_2);
  not not_16 (not_16_out, c);
  not not_17 (not_17_out, d);
  not not_18 (not_18_out, e);
  not not_19 (not_19_out, a);
  not not_20 (not_20_out, c);
  not not_21 (not_21_out, d);
  and and_27 (RF, a, not_15_out, not_16_out, not_17_out, not_18_out);
  and and_28 (LL, not_19_out, not_15_out, not_17_out, not_18_out, c);
  and and_29 (LR, d, not_18_out, not_19_out, not_15_out, not_20_out);
  and and_30 (RB, not_19_out, not_15_out, not_20_out, not_21_out, e);
  or or_9 (LF, RF, RB);
  and and_31 (LB, LF, LL, LR, RB, RF);

  assign RL = LL;
  assign RR = LR;

  // Notes on the sheet:
  //   L
  //   S
  //   R
  //   B
  //   //Move forward
  //   //Stop
  //   //Turn left
  //        //Turn right
  //   //Turn around
  //                                    //left_motor_forward
  //                         //left_motor_backward
  //                  //left_motor_right
  //              //left_motor_left
  //                       //right_motor_forward
  //                       //right_motor_backward
  //            //right_motor_right
  //          //right_motor_left
endmodule

// p
module path_generator (
  input  Button,
  input  Reset,
  output [3:0] _1_S,
  output [3:0] _2_L,
  output [3:0] _3_S,
  output [3:0] _4_R,
  output [3:0] _5_S,
  output [3:0] _6_L,
  output [3:0] _7_S,
  output [3:0] _8_L,
  output [4:0] Counter,
  output [3:0] _9_S,
  output [3:0] _10_B,
  output [3:0] LSRB,
  output [3:0] _11_S,
  output [3:0] _12_L,
  output [3:0] _13_S,
  output [3:0] _14_L,
  output [3:0] _15_S,
  output [3:0] _16_L,
  output [3:0] _17_S,
  output [3:0] _18_R,
  output [3:0] _19_S,
  output [3:0] _20_Stop
);

  wire decoder_1_out0, decoder_1_out1, decoder_1_out2, decoder_1_out3, decoder_1_out4, decoder_1_out5,
       decoder_1_out6, decoder_1_out7, decoder_1_out8, decoder_1_out9, decoder_1_out10, decoder_1_out11,
       decoder_1_out12, decoder_1_out13, decoder_1_out14, decoder_1_out15, decoder_1_out16, decoder_1_out17,
       decoder_1_out18, decoder_1_out19, decoder_1_out20, decoder_1_out21, decoder_1_out22, decoder_1_out23,
       decoder_1_out24, decoder_1_out25, decoder_1_out26, decoder_1_out27, decoder_1_out28, decoder_1_out29,
       decoder_1_out30, decoder_1_out31, or_1_out;
  wire [3:0] or_2_out, or_3_out, or_4_out, or_5_out;

  Decoder #(.select(5), .enable("false")) decoder_1 (
    .out0(decoder_1_out0), .out1(decoder_1_out1), .out2(decoder_1_out2), .out3(decoder_1_out3),
    .out4(decoder_1_out4), .out5(decoder_1_out5), .out6(decoder_1_out6), .out7(decoder_1_out7),
    .out8(decoder_1_out8), .out9(decoder_1_out9), .out10(decoder_1_out10), .out11(decoder_1_out11),
    .out12(decoder_1_out12), .out13(decoder_1_out13), .out14(decoder_1_out14), .out15(decoder_1_out15),
    .out16(decoder_1_out16), .out17(decoder_1_out17), .out18(decoder_1_out18), .out19(decoder_1_out19),
    .out20(decoder_1_out20), .out21(decoder_1_out21), .out22(decoder_1_out22), .out23(decoder_1_out23),
    .out24(decoder_1_out24), .out25(decoder_1_out25), .out26(decoder_1_out26), .out27(decoder_1_out27),
    .out28(decoder_1_out28), .out29(decoder_1_out29), .out30(decoder_1_out30), .out31(decoder_1_out31),
    .sel(Counter));
  Counter #(.width(5), .max('h1f), .ongoal("continue")) counter_1 (
    .Q(Counter), .clk(Button), .clr(Reset));  // open: load, D, count, carry
  or or_1 (or_1_out, decoder_1_out19, decoder_1_out20, decoder_1_out21, decoder_1_out22, decoder_1_out23, decoder_1_out24, decoder_1_out26, decoder_1_out27, decoder_1_out28, decoder_1_out29, decoder_1_out30, decoder_1_out31);
  Multiplexer #(.width(4), .enable("false")) multiplexer_1 (
    .in0(4'b0000), .in1(4'b0100), .out(_1_S), .sel(decoder_1_out0));
  Multiplexer #(.width(4), .enable("false")) multiplexer_2 (
    .in0(4'b0000), .in1(4'b1000), .out(_2_L), .sel(decoder_1_out1));
  Multiplexer #(.width(4), .enable("false")) multiplexer_3 (
    .in0(4'b0000), .in1(4'b0100), .out(_3_S), .sel(decoder_1_out2));
  Multiplexer #(.width(4), .enable("false")) multiplexer_4 (
    .in0(4'b0000), .in1(4'b0010), .out(_4_R), .sel(decoder_1_out3));
  Multiplexer #(.width(4), .enable("false")) multiplexer_5 (
    .in0(4'b0000), .in1(4'b0100), .out(_5_S), .sel(decoder_1_out4));
  Multiplexer #(.width(4), .enable("false")) multiplexer_6 (
    .in0(4'b0000), .in1(4'b1000), .out(_6_L), .sel(decoder_1_out5));
  Multiplexer #(.width(4), .enable("false")) multiplexer_7 (
    .in0(4'b0000), .in1(4'b0100), .out(_7_S), .sel(decoder_1_out6));
  Multiplexer #(.width(4), .enable("false")) multiplexer_8 (
    .in0(4'b0000), .in1(4'b1000), .out(_8_L), .sel(decoder_1_out7));
  Multiplexer #(.width(4), .enable("false")) multiplexer_9 (
    .in0(4'b0000), .in1(4'b0100), .out(_9_S), .sel(decoder_1_out8));
  Multiplexer #(.width(4), .enable("false")) multiplexer_10 (
    .in0(4'b0000), .in1(4'b0001), .out(_10_B), .sel(decoder_1_out9));
  Multiplexer #(.width(4), .enable("false")) multiplexer_11 (
    .in0(4'b0000), .in1(4'b0100), .out(_11_S), .sel(decoder_1_out10));
  Multiplexer #(.width(4), .enable("false")) multiplexer_12 (
    .in0(4'b0000), .in1(4'b1000), .out(_12_L), .sel(decoder_1_out11));
  Multiplexer #(.width(4), .enable("false")) multiplexer_13 (
    .in0(4'b0000), .in1(4'b0100), .out(_13_S), .sel(decoder_1_out12));
  Multiplexer #(.width(4), .enable("false")) multiplexer_14 (
    .in0(4'b0000), .in1(4'b1000), .out(_14_L), .sel(decoder_1_out13));
  Multiplexer #(.width(4), .enable("false")) multiplexer_15 (
    .in0(4'b0000), .in1(4'b0100), .out(_15_S), .sel(decoder_1_out14));
  Multiplexer #(.width(4), .enable("false")) multiplexer_16 (
    .in0(4'b0000), .in1(4'b1000), .out(_16_L), .sel(decoder_1_out15));
  Multiplexer #(.width(4), .enable("false")) multiplexer_17 (
    .in0(4'b0000), .in1(4'b0100), .out(_17_S), .sel(decoder_1_out16));
  Multiplexer #(.width(4), .enable("false")) multiplexer_18 (
    .in0(4'b0000), .in1(4'b0010), .out(_18_R), .sel(decoder_1_out17));
  Multiplexer #(.width(4), .enable("false")) multiplexer_19 (
    .in0(4'b0000), .in1(4'b0100), .out(_19_S), .sel(decoder_1_out18));
  Multiplexer #(.width(4), .enable("false")) multiplexer_20 (
    .in0(4'b0001), .in1(4'b0000), .out(_20_Stop), .sel(or_1_out));
  assign or_2_out = _1_S | _2_L | _3_S | _4_R | _5_S;  // OR_Gate or_2, 4 bits wide
  assign or_3_out = _6_L | _7_S | _8_L | _9_S | _10_B;  // OR_Gate or_3, 4 bits wide
  assign or_4_out = _11_S | _12_L | _13_S | _14_L | _15_S;  // OR_Gate or_4, 4 bits wide
  assign or_5_out = _16_L | _17_S | _18_R | _19_S | _20_Stop;  // OR_Gate or_5, 4 bits wide
  assign LSRB = or_2_out | or_3_out | or_4_out | or_5_out;  // OR_Gate or_6, 4 bits wide
endmodule

module path (
  input  Button_2,
  input  Reset_2,
  output S,
  output L,
  output S_2,
  output R,
  output S_3,
  output L_2,
  output S_4,
  output L_3,
  output S_5,
  output B,
  output S_6,
  output L_4,
  output S_7,
  output L_5,
  output S_8,
  output L_6,
  output S_9,
  output R_2,
  output S_10,
  output Stop
);

  wire [3:0] path_generator_1__1_s, path_generator_1__2_l, path_generator_1__3_s, path_generator_1__4_r,
       path_generator_1__5_s, path_generator_1__6_l, path_generator_1__7_s, path_generator_1__8_l,
       path_generator_1__9_s, path_generator_1__10_b, path_generator_1__11_s, path_generator_1__12_l,
       path_generator_1__13_s, path_generator_1__14_l, path_generator_1__15_s, path_generator_1__16_l,
       path_generator_1__17_s, path_generator_1__18_r, path_generator_1__19_s, path_generator_1__20_stop;

  path_generator path_generator_1 (
    .Button(Button_2), .Reset(Reset_2), ._1_S(path_generator_1__1_s), ._2_L(path_generator_1__2_l),
    ._3_S(path_generator_1__3_s), ._4_R(path_generator_1__4_r), ._5_S(path_generator_1__5_s),
    ._6_L(path_generator_1__6_l), ._7_S(path_generator_1__7_s), ._8_L(path_generator_1__8_l),
    ._9_S(path_generator_1__9_s), ._10_B(path_generator_1__10_b), ._11_S(path_generator_1__11_s),
    ._12_L(path_generator_1__12_l), ._13_S(path_generator_1__13_s), ._14_L(path_generator_1__14_l),
    ._15_S(path_generator_1__15_s), ._16_L(path_generator_1__16_l), ._17_S(path_generator_1__17_s),
    ._18_R(path_generator_1__18_r), ._19_S(path_generator_1__19_s), ._20_Stop(path_generator_1__20_stop));  // open: Counter, LSRB
  or or_1 (S, path_generator_1__1_s[0], path_generator_1__1_s[1], path_generator_1__1_s[2], path_generator_1__1_s[3]);
  or or_2 (L, path_generator_1__2_l[0], path_generator_1__2_l[1], path_generator_1__2_l[2], path_generator_1__2_l[3]);
  or or_3 (S_10, path_generator_1__19_s[3], path_generator_1__19_s[2], path_generator_1__19_s[1], path_generator_1__19_s[0]);
  nor nor_1 (Stop, path_generator_1__20_stop[3], path_generator_1__20_stop[2], path_generator_1__20_stop[1], path_generator_1__20_stop[0]);
  or or_4 (S_2, path_generator_1__3_s[0], path_generator_1__3_s[1], path_generator_1__3_s[2], path_generator_1__3_s[3]);
  or or_5 (R_2, path_generator_1__18_r[3], path_generator_1__18_r[2], path_generator_1__18_r[1], path_generator_1__18_r[0]);
  or or_6 (L_6, path_generator_1__16_l[3], path_generator_1__16_l[2], path_generator_1__16_l[1], path_generator_1__16_l[0]);
  or or_7 (S_9, path_generator_1__17_s[3], path_generator_1__17_s[2], path_generator_1__17_s[1], path_generator_1__17_s[0]);
  or or_8 (L_5, path_generator_1__14_l[3], path_generator_1__14_l[2], path_generator_1__14_l[1], path_generator_1__14_l[0]);
  or or_9 (S_8, path_generator_1__15_s[3], path_generator_1__15_s[2], path_generator_1__15_s[1], path_generator_1__15_s[0]);
  or or_10 (R, path_generator_1__4_r[0], path_generator_1__4_r[1], path_generator_1__4_r[2], path_generator_1__4_r[3]);
  or or_11 (S_7, path_generator_1__13_s[3], path_generator_1__13_s[2], path_generator_1__13_s[1], path_generator_1__13_s[0]);
  or or_12 (S_6, path_generator_1__11_s[3], path_generator_1__11_s[2], path_generator_1__11_s[1], path_generator_1__11_s[0]);
  or or_13 (L_4, path_generator_1__12_l[3], path_generator_1__12_l[2], path_generator_1__12_l[1], path_generator_1__12_l[0]);
  or or_14 (S_3, path_generator_1__5_s[0], path_generator_1__5_s[1], path_generator_1__5_s[2], path_generator_1__5_s[3]);
  or or_15 (B, path_generator_1__10_b[3], path_generator_1__10_b[2], path_generator_1__10_b[1], path_generator_1__10_b[0]);
  or or_16 (L_3, path_generator_1__8_l[3], path_generator_1__8_l[2], path_generator_1__8_l[1], path_generator_1__8_l[0]);
  or or_17 (S_5, path_generator_1__9_s[3], path_generator_1__9_s[2], path_generator_1__9_s[1], path_generator_1__9_s[0]);
  or or_18 (S_4, path_generator_1__7_s[3], path_generator_1__7_s[2], path_generator_1__7_s[1], path_generator_1__7_s[0]);
  or or_19 (L_2, path_generator_1__6_l[0], path_generator_1__6_l[1], path_generator_1__6_l[2], path_generator_1__6_l[3]);
endmodule
